// Logisim project test1.circ as structural Verilog: 1 circuit, main circuit main
module main (
  output out_1
);

  wire A_out, and_1_out, and_2_out, B_out, C_out, D_out;

  Clock sysclk ();  // open: out
  Clock A (.out(A_out));
  Clock B (.out(B_out));
  Clock C (.out(C_out));
  Clock D (.out(D_out));
  and and_1 (and_1_out, A_out, B_out);
  and and_2 (and_2_out, C_out, ~D_out);  // AND_Gate
  or or_1 (out_1, and_1_out, and_2_out);
endmodule
