// Logisim project test5.circ as structural Verilog: 1 circuit, main circuit main
module main (
  input  A,
  input  B,
  input  C,
  input  D,
  output out_5
);

  wire nand_1_out, nand_2_out;

  nand nand_1 (nand_1_out, ~C, D);  // NAND_Gate
  nand nand_2 (nand_2_out, B, C, ~D);  // NAND_Gate
  nand nand_3 (out_5, nand_1_out, nand_2_out);
endmodule
